# Fritzing sketch Password (saved by Fritzing 0.9.2b)
circuit board: 9.16356cm x 3.00418cm
breadboards: 1

parts:
  IC2 = 24LC128 [part_number=24C04 package=THT]
  X1 = USB Connectors [package=usb-a-h]
  R9 = Resistor [tolerance=±5% resistance=68 package=THT]
  R10 = Resistor [tolerance=±5% resistance=68 package=THT]
  S1 = Round Pushbutton
  R5 = Resistor [tolerance=±5% resistance=1k package=THT]
  R8 = Resistor [tolerance=±5% resistance=2.2k package=THT]
  Q2 = PNP-Transistor [part_number=BC327 package="TO92 [THT]"]
  Q1 = PNP-Transistor [part_number=BC327 package="TO92 [THT]"]
  Q3 = PNP-Transistor [part_number=BC327 package="TO92 [THT]"]
  Q4 = PNP-Transistor [part_number=BC327 package="TO92 [THT]"]
  IC3 = ULN2803A [package=THT]
  U1 = 7-SEGMENT-4DIGIT-YOUNGSUN [package=7-segment-4digit-youngsun-longpads]
  R1 = Resistor [tolerance=±5% resistance=2.2k package=THT]
  R2 = Resistor [tolerance=±5% resistance=2.2k package=THT]
  R3 = Resistor [tolerance=±5% resistance=2.2k package=THT]
  R11 = Resistor [tolerance=±5% resistance=1.5k package=THT]
  R4 = Resistor [tolerance=±5% resistance=1k package=THT]
  D2 = Zener Diode [part_number=1N4732A breakdown_voltage=3.6V package="300 mil [THT]"]
  R6 = Resistor [tolerance=±5% resistance=1k package=THT]
  R7 = Resistor [tolerance=±5% resistance=1k package=THT]
  D1 = Zener Diode [part_number=1N4732A breakdown_voltage=3.6V package="300 mil [THT]"]
  IC1 = ATTiny2313 [part_number="ATtiny 2313" package=THT]

nets:
  N1: IC2.A0, R3.Pin_1
  N2: IC2.A1, R2.Pin_1
  N3: IC2.A2, R1.Pin_1
  GND: IC2.0V, X1.GND, IC3.0V, R1.Pin_0, R2.Pin_0, R3.Pin_0, D2.anode, D1.anode, IC1.GND
  N4: IC2.SDA_-_I2C_Data, IC1.PB5
  N5: IC2.SCL_-_I2C_Clock, IC1.PB7
  N6: IC2.WP_-_Write_Protect, R8.Pin_0
  5V: IC2.+V, X1.VBUS, S1.leg0, R8.Pin_1, Q2.E, Q1.E, Q3.E, Q4.E, R11.Pin_1, IC1.VCC
  N7: X1.D-, R10.Pin_1, R11.Pin_0, D2.cathode
  N8: X1.D+, R9.Pin_1, D1.cathode
  N9: R9.Pin_0, IC1.PB6
  N10: R10.Pin_0, IC1.PB4
  N11: S1.leg1, IC1.PD0
  N12: R5.Pin_0, IC1.PB0
  N13: R5.Pin_1, Q2.B
  N14: Q2.C, U1.DIG2
  N15: Q1.B, R4.Pin_1
  N16: Q1.C, U1.DIG1
  N17: Q3.B, R6.Pin_1
  N18: Q3.C, U1.DIG3
  N19: Q4.B, R7.Pin_1
  N20: Q4.C, U1.DIG4
  N21: IC3.In_1, IC1.PB2
  N22: IC3.In_2, IC1.PD5
  N23: IC3.In_3, IC1.PD4
  N24: IC3.In_4, IC1.PD3
  N25: IC3.In_5, IC1.PD2
  N26: IC3.In_6, IC1.PA0
  N27: IC3.In_7, IC1.PA1
  N28: IC3.In_8, IC1.PD1
  N29: IC3.Out_8, U1.DP
  N30: IC3.Out_7, U1.B
  N31: IC3.Out_6, U1.G
  N32: IC3.Out_5, U1.A
  N33: IC3.Out_4, U1.C
  N34: IC3.Out_3, U1.F
  N35: IC3.Out_2, U1.E
  N36: IC3.Out_1, U1.D
  N37: R4.Pin_0, IC1.PB1
  N38: R6.Pin_0, IC1.PB3
  N39: R7.Pin_0, IC1.PD6

notes:
  Password Storage, A deniable storage for 16 passwords with hardware PIN and USB-HID, 1
